# Fritzing sketch SimpleStrobe (saved by Fritzing 0.9.3b)
circuit board: 8.46667cm x 5.64444cm
breadboards: 1

parts:
  Part1 = Arduino Uno (Rev3)
  R1 = Rotary Potentiometer (Small) [maximum_resistance=100kΩ package=THT]
  LED1 = LED - 5mm [color="Red (633nm)" package="5 mm [THT]"]

nets:
  N1: Part1.A0, R1.wiper
  N2: Part1.D13/SCK, LED1.anode
  N3: Part1.GND, R1.leg2, LED1.cathode
  N4: Part1.5V, R1.leg1
